# Fritzing sketch Retractable_Joystick_Schematics (saved by Fritzing 0.9.3b)
breadboards: 1

parts:
  IC1 = L293D [package=THT]
  Part2 = Arduino Nano (Rev3.0)
  S3 = Pushbutton [part_number=Left/Right package=THT]
  S4 = Pushbutton [part_number="Retract & Extend" package=THT]
  S5 = Pushbutton [part_number="Limit Switch" package=THT]
  R5 = Resistor [tolerance=±5% resistance=270 package=THT]
  R6 = Resistor [tolerance=±5% resistance=270 package=THT]
  R7 = Resistor [tolerance=±5% resistance=270 package=THT]
  M2 = DC Motor

nets:
  N1: IC1.Enable_1, Part2.D3
  N2: IC1.In_1, Part2.D5
  N3: IC1.Out_1_(_Controlled_by_Enable_1_), M2.pin_2
  N4: IC1.0V, Part2.GND, R5.Pin_0, R6.Pin_0, R7.Pin_0
  N5: IC1.Out_2_(_Controlled_by_Enable_1_), M2.pin_1
  N6: IC1.In_2, Part2.D6
  N7: IC1.+Vmotor, IC1.+V, Part2.5V, S3.leg1, S4.leg1, S5.leg1
  N8: Part2.D4, S3.leg0, R7.Pin_1
  N9: Part2.D7, S4.leg0, R5.Pin_1
  N10: Part2.D8, S5.leg0, R6.Pin_1
